# Fritzing sketch Untitled Sketch (saved by Fritzing 1.0.2b)
breadboards: 1

parts:
  Part1 = Arduino Uno (Rev3) - ICSP
  Disp1 = 20mm 8x8 dot matrix column cathode led display with standard pcb pads
  R1 = Resistor [tolerance=±5% resistance=220 package="2010 [SMD]"]
  R2 = Resistor [tolerance=±5% resistance=220 package="2010 [SMD]"]
  R3 = Resistor [tolerance=±5% resistance=220 package="2010 [SMD]"]
  R4 = Resistor [tolerance=±5% resistance=220 package="2010 [SMD]"]
  R5 = Resistor [tolerance=±5% resistance=220 package="2010 [SMD]"]
  R6 = Resistor [tolerance=±5% resistance=220 package="2010 [SMD]"]
  R7 = Resistor [tolerance=±5% resistance=220 package="2010 [SMD]"]
  R8 = Resistor [tolerance=±5% resistance=220 package="2010 [SMD]"]

nets:
  N1: Part1.A0, Disp1.pin_6
  N2: Part1.A1, Disp1.pin_11
  N3: Part1.A2, Disp1.pin_15
  N4: Part1.A3, Disp1.pin_16
  N5: Part1.D8, R7.Pin_0
  N6: Part1.D9_PWM, R8.Pin_0
  N7: Part1.D10_PWM/SS, Disp1.pin_13
  N8: Part1.D11_PWM/MOSI, Disp1.pin_3
  N9: Part1.D12/MISO, Disp1.pin_4
  N10: Part1.D13/SCK, Disp1.pin_10
  N11: Part1.D2, R1.Pin_1
  N12: Part1.D3_PWM, R2.Pin_0
  N13: Part1.D4, R3.Pin_1
  N14: Part1.D5_PWM, R4.Pin_1
  N15: Part1.D6_PWM, R5.Pin_0
  N16: Part1.D7, R6.Pin_1
  N17: Disp1.pin_1, R5.Pin_1
  N18: Disp1.pin_2, R7.Pin_1
  N19: Disp1.pin_5, R8.Pin_1
  N20: Disp1.pin_7, R6.Pin_0
  N21: Disp1.pin_8, R3.Pin_0
  N22: Disp1.pin_9, R1.Pin_0
  N23: Disp1.pin_12, R4.Pin_0
  N24: Disp1.pin_14, R2.Pin_1
